// Logisim project ALU.circ as structural Verilog: 3 circuits, main circuit ALU
module ALU (
  input  [31:0] A,
  input  [31:0] B,
  input  [3:0] Sel,
  output [31:0] HI,
  output [31:0] Out___LO,
  output Z,
  output N
);

  wire and_2_out, comparator_1_lt, comparator_2_lt;
  wire [31:0] ADD, AND, DIV_HI, DIV_LO, DIVU_HI, DIVU_LO, MUL_HI, MUL_LO, MULU_HI, MULU_LO, NOR, OR, SLT,
       SLTU, SUB, XOR;

  assign AND = A & B;  // AND_Gate and_1, 32 bits wide
  assign OR = A | B;  // OR_Gate or_1, 32 bits wide
  assign NOR = ~(A | B);  // NOR_Gate nor_1, 32 bits wide
  assign XOR = A ^ B;  // XOR_Gate xor_1, 32 bits wide
  Comparator #(.width(32)) comparator_1 (.a(A), .b(B), .lt(comparator_1_lt));  // open: gt, eq
  Comparator #(.width(32), .mode("unsigned")) comparator_2 (.a(A), .b(B), .lt(comparator_2_lt));  // open: gt, eq
  Adder #(.width(32)) adder_1 (.a(A), .b(B), .out(ADD));  // open: cin, cout
  Subtractor #(.width(32)) subtractor_1 (.a(A), .b(B), .out(SUB));  // open: bin, bout
  assign SLT = {{31{1'b0}}, comparator_1_lt};  // Bit_Extender bit_extender_1
  assign SLTU = {{31{1'b0}}, comparator_2_lt};  // Bit_Extender bit_extender_2
  Multiplier #(.width(32)) multiplier_1 (.a(A), .b(B), .out(MUL_LO), .cout(MUL_HI));  // open: cin
  MULU mulu_1 (.A(A), .B(B), .HI(MULU_HI), .LO(MULU_LO));
  Divider #(.width(32)) divider_1 (.a(A), .b(B), .out(DIV_LO), .rem(DIV_HI));  // open: upper
  DIVU divu_1 (.A(A), .B(B), .HI(DIVU_HI), .LO(DIVU_LO));
  Multiplexer #(.select(4), .width(32), .enable("false")) multiplexer_1 (
    .in0(AND), .in1(OR), .in2(NOR), .in3(XOR), .in4(SLT), .in5(SLTU), .in6(ADD), .in7(SUB), .in8(MUL_LO),
    .in9(MULU_LO), .in10(DIV_LO), .in11(DIVU_LO), .out(Out___LO), .sel(Sel));  // open: in12, in13, in14, in15
  Multiplexer #(.select(2), .width(32), .enable("false")) multiplexer_2 (
    .in0(MUL_HI), .in1(MULU_HI), .in2(DIV_HI), .in3(DIVU_HI), .out(HI), .sel(Sel[3:2]));
  and and_2 (and_2_out, Sel[0], ~Sel[1]);  // AND_Gate
  Comparator #(.width(32)) comparator_3 (.a(Out___LO), .b({32{1'b0}}), .eq(Z), .lt(N));  // open: gt

  // Notes on the sheet:
  //   ALU
endmodule

module MULU (
  input  [31:0] A,
  input  [31:0] B,
  output [31:0] HI,
  output [31:0] LO
);

  wire [31:0] adder_1_out, C_IN, multiplexer_1_out, multiplexer_2_out;

  Multiplier #(.width(32)) multiplier_1 (.a(A), .b(B), .out(LO), .cout(C_IN));  // open: cin
  Multiplexer #(.width(32), .enable("false")) multiplexer_1 (
    .in0({32{1'b0}}), .in1(A), .out(multiplexer_1_out), .sel(A[31]));
  Multiplexer #(.width(32), .enable("false")) multiplexer_2 (
    .in0({32{1'b0}}), .in1(B), .out(multiplexer_2_out), .sel(B[31]));
  Adder #(.width(32)) adder_1 (.a(multiplexer_1_out), .b(multiplexer_2_out), .out(adder_1_out));  // open: cin, cout
  Adder #(.width(32)) adder_2 (.a(C_IN), .b(adder_1_out), .out(HI));  // open: cin, cout

  // Notes on the sheet:
  //   UNSIGNED MULTIPLICATION
endmodule

module DIVU (
  input  [31:0] A,
  input  [31:0] B,
  output [31:0] HI,
  output [31:0] LO
);

  wire NEGATIVE;
  wire [31:0] A___B, A___B_t, minus_A, minus_B, multiplexer_1_out, multiplexer_2_out;

  Negator #(.width(32)) negator_1 (.in(A), .out(minus_A));
  Negator #(.width(32)) negator_2 (.in(B), .out(minus_B));
  Multiplexer #(.width(32), .enable("false")) multiplexer_1 (
    .in0(A), .in1(minus_A), .out(multiplexer_1_out), .sel(A[31]));
  Multiplexer #(.width(32), .enable("false")) multiplexer_2 (
    .in0(B), .in1(minus_B), .out(multiplexer_2_out), .sel(B[31]));
  Divider #(.width(32)) divider_1 (
    .a(multiplexer_1_out), .b(multiplexer_2_out), .out(A___B_t), .rem(HI));  // open: upper
  xor xor_1 (NEGATIVE, A[31], B[31]);
  Multiplexer #(.width(32), .enable("false")) multiplexer_3 (.in0(A___B_t), .in1(A___B), .out(LO), .sel(NEGATIVE));
  Negator #(.width(32)) negator_3 (.in(A___B_t), .out(A___B));

  // Other names for the same wires on the sheet: A_31 = A[31]; B_31 = B[31]

  // Notes on the sheet:
  //   UNSIGNED DIVISION
endmodule
