// Logisim project Branch Control.circ as structural Verilog: 1 circuit, main circuit Branch Control
module Branch_Control (
  input  [25:0] DEST,
  input  [31:0] PC,
  input  [31:0] Rs,
  input  [31:0] Rt,
  input  [15:0] OFFSET,
  input  [7:0] Op_code,
  output [31:0] BC_OUT
);

  wire and_1_out, and_2_out, and_3_out, and_4_out, and_5_out, and_6_out, comparator_1_eq, or_2_out, or_3_out,
       Rs___0, Rs____0, Rs____Rt;
  wire [1:0] priority_encoder_1_out;
  wire [31:0] PC___4, PC___4___4___OFFSET;
  wire [31:18] OFFSET___4;

  or or_1 (Rs____0, comparator_1_eq, Rs___0);
  Comparator #(.width(32)) comparator_1 (.a(Rs), .b({32{1'b0}}), .eq(comparator_1_eq), .lt(Rs___0));  // open: gt
  Comparator #(.width(32)) comparator_2 (.a(Rs), .b(Rt), .eq(Rs____Rt));  // open: gt, lt
  Adder #(.width(32)) adder_1 (.a(PC), .b(32'h4), .out(PC___4));  // open: cin, cout
  Adder #(.width(32)) adder_2 (
    .a(PC___4), .b({OFFSET___4, OFFSET, 2'b00}), .out(PC___4___4___OFFSET));  // open: cin, cout
  and and_1 (and_1_out, Op_code[1], Rs____Rt);
  and and_2 (and_2_out, ~Rs____Rt, Op_code[2]);  // AND_Gate
  and and_3 (and_3_out, Op_code[3], Rs____0);
  and and_4 (and_4_out, ~Rs____0, Op_code[4]);  // AND_Gate
  and and_5 (and_5_out, Op_code[5], Rs___0);
  or or_2 (or_2_out, and_1_out, and_2_out, and_3_out, and_4_out, and_5_out);
  or or_3 (or_3_out, 1'b1, Op_code[0]);
  and and_6 (and_6_out, or_2_out, ~Op_code[0]);  // AND_Gate
  assign OFFSET___4 = {{13{OFFSET[15]}}, OFFSET[15]};  // Bit_Extender bit_extender_1
  Priority_Encoder #(.select(2)) priority_encoder_1 (
    .in0(or_3_out), .in1(and_6_out), .in2(Op_code[6]), .in3(Op_code[7]), .out(priority_encoder_1_out));  // open: gs, en_out, en_in
  Multiplexer #(.select(2), .width(32), .enable("false")) multiplexer_1 (
    .in0(PC___4), .in1(PC___4___4___OFFSET), .in2({PC[31:28], DEST, 2'b00}), .in3(Rs), .out(BC_OUT),
    .sel(priority_encoder_1_out));

  // Other names for the same wires on the sheet: JMP[31:2] = {PC[31:28], DEST}; OFFSET___4[17:2] = OFFSET;
  //   NOP = Op_code[0]; BEQ = Op_code[1]; BNE = Op_code[2]; BLEZ = Op_code[3]; BGTZ = Op_code[4]; BLTZ = Op_code[5];
  //   J = Op_code[6]; JR = Op_code[7]
endmodule
