// Logisim project Cache.circ as structural Verilog: 1 circuit, main circuit Cache
module Cache (
  input  clk,
  input  reset,
  input  Data_ready,
  input  Inst_ready,
  input  CS,
  input  nR_W,
  input  Invalidate_cache_address,
  input  [15:0] Address,
  input  [31:0] RAM_Out_0,
  input  [31:0] RAM_Out_1,
  input  [31:0] RAM_Out_2,
  input  [31:0] RAM_Out_3,
  output Contains_current_address,
  output [31:0] Cache_Out_0,
  output [31:0] Cache_Out_1,
  output [31:0] Cache_Out_2,
  output [31:0] Cache_Out_3
);

  wire en0, en1, en2, en3, en4, en5, en6, en7, en8, en9, en10, en11, en12, en13, en14, en15, Enable,
       Invalid_0, Invalid_1, Invalid_2, Invalid_3, Invalid_4, Invalid_5, Invalid_6, Invalid_7, Invalid_8,
       Invalid_9, Invalid_10, Invalid_11, Invalid_12, Invalid_13, Invalid_14, Invalid_15, or_1_out, or_2_out,
       or_3_out, or_4_out, or_5_out, or_6_out, or_7_out, or_8_out, or_9_out, or_10_out, or_11_out, or_12_out,
       or_13_out, or_14_out, or_15_out, or_16_out, or_17_out, or_18_out, Valid_0, Valid_1, Valid_2, Valid_3,
       Valid_4, Valid_5, Valid_6, Valid_7, Valid_8, Valid_9, Valid_10, Valid_11, Valid_12, Valid_13,
       Valid_14, Valid_15, Valid_Data_in_index, Valid_Tag;
  wire [11:0] Cache_tag, Tag_0, Tag_1, Tag_2, Tag_3, Tag_4, Tag_5, Tag_6, Tag_7, Tag_8, Tag_9, Tag_10,
       Tag_11, Tag_12, Tag_13, Tag_14, Tag_15;
  wire [31:0] _0_0, _0_1, _0_2, _0_3, _0_4, _0_5, _0_6, _0_7, _0_8, _0_9, _0_10, _0_11, _0_12, _0_13, _0_14,
       _0_15, _1_0, _1_1, _1_2, _1_3, _1_4, _1_5, _1_6, _1_7, _1_8, _1_9, _1_10, _1_11, _1_12, _1_13, _1_14,
       _1_15, _2_0, _2_1, _2_2, _2_3, _2_4, _2_5, _2_6, _2_7, _2_8, _2_9, _2_10, _2_11, _2_12, _2_13, _2_14,
       _2_15, _3_0, _3_1, _3_2, _3_3, _3_4, _3_5, _3_6, _3_7, _3_8, _3_9, _3_10, _3_11, _3_12, _3_13, _3_14,
       _3_15;

  Multiplexer #(.select(4), .width(32), .disabled(0), .enable("false")) multiplexer_1 (
    .in0(_0_0), .in1(_0_1), .in2(_0_2), .in3(_0_3), .in4(_0_4), .in5(_0_5), .in6(_0_6), .in7(_0_7),
    .in8(_0_8), .in9(_0_9), .in10(_0_10), .in11(_0_11), .in12(_0_12), .in13(_0_13), .in14(_0_14),
    .in15(_0_15), .out(Cache_Out_0), .sel(Address[3:0]));
  Multiplexer #(.select(4), .width(32), .disabled(0), .enable("false")) multiplexer_2 (
    .in0(_1_0), .in1(_1_1), .in2(_1_2), .in3(_1_3), .in4(_1_4), .in5(_1_5), .in6(_1_6), .in7(_1_7),
    .in8(_1_8), .in9(_1_9), .in10(_1_10), .in11(_1_11), .in12(_1_12), .in13(_1_13), .in14(_1_14),
    .in15(_1_15), .out(Cache_Out_1), .sel(Address[3:0]));
  Multiplexer #(.select(4), .width(32), .disabled(0), .enable("false")) multiplexer_3 (
    .in0(_2_0), .in1(_2_1), .in2(_2_2), .in3(_2_3), .in4(_2_4), .in5(_2_5), .in6(_2_6), .in7(_2_7),
    .in8(_2_8), .in9(_2_9), .in10(_2_10), .in11(_2_11), .in12(_2_12), .in13(_2_13), .in14(_2_14),
    .in15(_2_15), .out(Cache_Out_2), .sel(Address[3:0]));
  Multiplexer #(.select(4), .width(32), .disabled(0), .enable("false")) multiplexer_4 (
    .in0(_3_0), .in1(_3_1), .in2(_3_2), .in3(_3_3), .in4(_3_4), .in5(_3_5), .in6(_3_6), .in7(_3_7),
    .in8(_3_8), .in9(_3_9), .in10(_3_10), .in11(_3_11), .in12(_3_12), .in13(_3_13), .in14(_3_14),
    .in15(_3_15), .out(Cache_Out_3), .sel(Address[3:0]));
  or or_1 (or_1_out, Inst_ready, Data_ready);
  and and_1 (Enable, ~nR_W, or_1_out, CS);  // AND_Gate
  and and_2 (Contains_current_address, Valid_Data_in_index, Valid_Tag);
  Comparator #(.width(12)) comparator_1 (.a(Cache_tag), .b(Address[15:4]), .eq(Valid_Tag));  // open: gt, lt
  Demultiplexer #(.select(4), .enable("false")) demultiplexer_1 (
    .out0(en0), .out1(en1), .out2(en2), .out3(en3), .out4(en4), .out5(en5), .out6(en6), .out7(en7),
    .out8(en8), .out9(en9), .out10(en10), .out11(en11), .out12(en12), .out13(en13), .out14(en14),
    .out15(en15), .in(Enable), .sel(Address[3:0]));
  Multiplexer #(.select(4), .width(12), .enable("false")) multiplexer_5 (
    .in0(Tag_0), .in1(Tag_1), .in2(Tag_2), .in3(Tag_3), .in4(Tag_4), .in5(Tag_5), .in6(Tag_6), .in7(Tag_7),
    .in8(Tag_8), .in9(Tag_9), .in10(Tag_10), .in11(Tag_11), .in12(Tag_12), .in13(Tag_13), .in14(Tag_14),
    .in15(Tag_15), .out(Cache_tag), .sel(Address[3:0]));
  Multiplexer #(.select(4), .disabled(0), .enable("false")) multiplexer_6 (
    .in0(Valid_0), .in1(Valid_1), .in2(Valid_2), .in3(Valid_3), .in4(Valid_4), .in5(Valid_5), .in6(Valid_6),
    .in7(Valid_7), .in8(Valid_8), .in9(Valid_9), .in10(Valid_10), .in11(Valid_11), .in12(Valid_12),
    .in13(Valid_13), .in14(Valid_14), .in15(Valid_15), .out(Valid_Data_in_index), .sel(Address[3:0]));
  Demultiplexer #(.select(4), .enable("false")) demultiplexer_2 (
    .out0(Invalid_0), .out1(Invalid_1), .out2(Invalid_2), .out3(Invalid_3), .out4(Invalid_4),
    .out5(Invalid_5), .out6(Invalid_6), .out7(Invalid_7), .out8(Invalid_8), .out9(Invalid_9),
    .out10(Invalid_10), .out11(Invalid_11), .out12(Invalid_12), .out13(Invalid_13), .out14(Invalid_14),
    .out15(Invalid_15), .in(or_2_out), .sel(Address[3:0]));
  or or_2 (or_2_out, Invalidate_cache_address, reset);
  D_Flip_Flop #(.trigger("falling")) d_ff_1 (
    .clk(clk), .D(or_3_out), .Q(Valid_0), .reset(Invalid_0));  // open: Qn, preset, en
  or or_3 (or_3_out, Valid_0, en0);
  D_Flip_Flop #(.trigger("falling")) d_ff_2 (
    .clk(clk), .D(or_4_out), .Q(Valid_1), .reset(Invalid_1));  // open: Qn, preset, en
  or or_4 (or_4_out, Valid_1, en1);
  D_Flip_Flop #(.trigger("falling")) d_ff_3 (
    .clk(clk), .D(or_5_out), .Q(Valid_2), .reset(Invalid_2));  // open: Qn, preset, en
  buf or_5 (or_5_out, Valid_2);  // OR_Gate
  D_Flip_Flop #(.trigger("falling")) d_ff_4 (
    .clk(clk), .D(or_6_out), .Q(Valid_3), .reset(Invalid_3));  // open: Qn, preset, en
  or or_6 (or_6_out, Valid_3, en3);
  D_Flip_Flop #(.trigger("falling")) d_ff_5 (
    .clk(clk), .D(or_7_out), .Q(Valid_4), .reset(Invalid_4));  // open: Qn, preset, en
  or or_7 (or_7_out, Valid_4, en4);
  D_Flip_Flop #(.trigger("falling")) d_ff_6 (
    .clk(clk), .D(or_8_out), .Q(Valid_5), .reset(Invalid_5));  // open: Qn, preset, en
  or or_8 (or_8_out, Valid_5, en5);
  D_Flip_Flop #(.trigger("falling")) d_ff_7 (
    .clk(clk), .D(or_9_out), .Q(Valid_6), .reset(Invalid_6));  // open: Qn, preset, en
  buf or_9 (or_9_out, Valid_6);  // OR_Gate
  D_Flip_Flop #(.trigger("falling")) d_ff_8 (
    .clk(clk), .D(or_10_out), .Q(Valid_7), .reset(Invalid_7));  // open: Qn, preset, en
  or or_10 (or_10_out, Valid_7, en7);
  D_Flip_Flop #(.trigger("falling")) d_ff_9 (
    .clk(clk), .D(or_11_out), .Q(Valid_8), .reset(Invalid_8));  // open: Qn, preset, en
  or or_11 (or_11_out, Valid_8, en8);
  D_Flip_Flop #(.trigger("falling")) d_ff_10 (
    .clk(clk), .D(or_12_out), .Q(Valid_9), .reset(Invalid_9));  // open: Qn, preset, en
  or or_12 (or_12_out, Valid_9, en9);
  D_Flip_Flop #(.trigger("falling")) d_ff_11 (
    .clk(clk), .D(or_13_out), .Q(Valid_10), .reset(Invalid_10));  // open: Qn, preset, en
  or or_13 (or_13_out, Valid_10, en10);
  D_Flip_Flop #(.trigger("falling")) d_ff_12 (
    .clk(clk), .D(or_14_out), .Q(Valid_11), .reset(Invalid_11));  // open: Qn, preset, en
  or or_14 (or_14_out, Valid_11, en11);
  D_Flip_Flop #(.trigger("falling")) d_ff_13 (
    .clk(clk), .D(or_15_out), .Q(Valid_12), .reset(Invalid_12));  // open: Qn, preset, en
  or or_15 (or_15_out, Valid_12, en12);
  D_Flip_Flop #(.trigger("falling")) d_ff_14 (
    .clk(clk), .D(or_16_out), .Q(Valid_13), .reset(Invalid_13));  // open: Qn, preset, en
  or or_16 (or_16_out, Valid_13, en13);
  D_Flip_Flop #(.trigger("falling")) d_ff_15 (
    .clk(clk), .D(or_17_out), .Q(Valid_14), .reset(Invalid_14));  // open: Qn, preset, en
  or or_17 (or_17_out, Valid_14, en14);
  D_Flip_Flop #(.trigger("falling")) d_ff_16 (
    .clk(clk), .D(or_18_out), .Q(Valid_15), .reset(Invalid_15));  // open: Qn, preset, en
  or or_18 (or_18_out, Valid_15, en15);
  Register #(.width(12)) T0 (.D(Address[15:4]), .en(en0), .Q(Tag_0), .clk(clk), .clr(reset));
  Register #(.width(12)) T1 (.D(Address[15:4]), .en(en1), .Q(Tag_1), .clk(clk), .clr(reset));
  Register #(.width(12)) T2 (.D(Address[15:4]), .en(en2), .Q(Tag_2), .clk(clk), .clr(reset));
  Register #(.width(12)) T3 (.D(Address[15:4]), .en(en3), .Q(Tag_3), .clk(clk), .clr(reset));
  Register #(.width(12)) T4 (.D(Address[15:4]), .en(en4), .Q(Tag_4), .clk(clk), .clr(reset));
  Register #(.width(12)) T5 (.D(Address[15:4]), .en(en5), .Q(Tag_5), .clk(clk), .clr(reset));
  Register #(.width(12)) T6 (.D(Address[15:4]), .en(en6), .Q(Tag_6), .clk(clk), .clr(reset));
  Register #(.width(12)) T7 (.D(Address[15:4]), .en(en7), .Q(Tag_7), .clk(clk), .clr(reset));
  Register #(.width(12)) T8 (.D(Address[15:4]), .en(en8), .Q(Tag_8), .clk(clk), .clr(reset));
  Register #(.width(12)) T9 (.D(Address[15:4]), .en(en9), .Q(Tag_9), .clk(clk), .clr(reset));
  Register #(.width(12)) T10 (.D(Address[15:4]), .en(en10), .Q(Tag_10), .clk(clk), .clr(reset));
  Register #(.width(12)) T11 (.D(Address[15:4]), .en(en11), .Q(Tag_11), .clk(clk), .clr(reset));
  Register #(.width(12)) T12 (.D(Address[15:4]), .en(en12), .Q(Tag_12), .clk(clk), .clr(reset));
  Register #(.width(12)) T13 (.D(Address[15:4]), .en(en13), .Q(Tag_13), .clk(clk), .clr(reset));
  Register #(.width(12)) T14 (.D(Address[15:4]), .en(en14), .Q(Tag_14), .clk(clk), .clr(reset));
  Register #(.width(12)) T15 (.D(Address[15:4]), .en(en15), .Q(Tag_15), .clk(clk), .clr(reset));
  Register #(.width(32)) C0_0 (.D(RAM_Out_0), .en(en0), .Q(_0_0), .clk(clk), .clr(reset));
  Register #(.width(32)) C0_1 (.D(RAM_Out_0), .en(en1), .Q(_0_1), .clk(clk), .clr(reset));
  Register #(.width(32)) C0_2 (.D(RAM_Out_0), .en(en2), .Q(_0_2), .clk(clk), .clr(reset));
  Register #(.width(32)) C0_3 (.D(RAM_Out_0), .en(en3), .Q(_0_3), .clk(clk), .clr(reset));
  Register #(.width(32)) C0_4 (.D(RAM_Out_0), .en(en4), .Q(_0_4), .clk(clk), .clr(reset));
  Register #(.width(32)) C0_5 (.D(RAM_Out_0), .en(en5), .Q(_0_5), .clk(clk), .clr(reset));
  Register #(.width(32)) C0_6 (.D(RAM_Out_0), .en(en6), .Q(_0_6), .clk(clk), .clr(reset));
  Register #(.width(32)) C0_7 (.D(RAM_Out_0), .en(en7), .Q(_0_7), .clk(clk), .clr(reset));
  Register #(.width(32)) C0_8 (.D(RAM_Out_0), .en(en8), .Q(_0_8), .clk(clk), .clr(reset));
  Register #(.width(32)) C0_9 (.D(RAM_Out_0), .en(en9), .Q(_0_9), .clk(clk), .clr(reset));
  Register #(.width(32)) C0_10 (.D(RAM_Out_0), .en(en10), .Q(_0_10), .clk(clk), .clr(reset));
  Register #(.width(32)) C0_11 (.D(RAM_Out_0), .en(en11), .Q(_0_11), .clk(clk), .clr(reset));
  Register #(.width(32)) C0_12 (.D(RAM_Out_0), .en(en12), .Q(_0_12), .clk(clk), .clr(reset));
  Register #(.width(32)) C0_13 (.D(RAM_Out_0), .en(en13), .Q(_0_13), .clk(clk), .clr(reset));
  Register #(.width(32)) C0_14 (.D(RAM_Out_0), .en(en14), .Q(_0_14), .clk(clk), .clr(reset));
  Register #(.width(32)) C0_15 (.D(RAM_Out_0), .en(en15), .Q(_0_15), .clk(clk), .clr(reset));
  Register #(.width(32)) C1_0 (.D(RAM_Out_1), .en(en0), .Q(_1_0), .clk(clk), .clr(reset));
  Register #(.width(32)) C1_1 (.D(RAM_Out_1), .en(en1), .Q(_1_1), .clk(clk), .clr(reset));
  Register #(.width(32)) C1_2 (.D(RAM_Out_1), .en(en2), .Q(_1_2), .clk(clk), .clr(reset));
  Register #(.width(32)) C1_3 (.D(RAM_Out_1), .en(en3), .Q(_1_3), .clk(clk), .clr(reset));
  Register #(.width(32)) C1_4 (.D(RAM_Out_1), .en(en4), .Q(_1_4), .clk(clk), .clr(reset));
  Register #(.width(32)) C1_5 (.D(RAM_Out_1), .en(en5), .Q(_1_5), .clk(clk), .clr(reset));
  Register #(.width(32)) C1_6 (.D(RAM_Out_1), .en(en6), .Q(_1_6), .clk(clk), .clr(reset));
  Register #(.width(32)) C1_7 (.D(RAM_Out_1), .en(en7), .Q(_1_7), .clk(clk), .clr(reset));
  Register #(.width(32)) C1_8 (.D(RAM_Out_1), .en(en8), .Q(_1_8), .clk(clk), .clr(reset));
  Register #(.width(32)) C1_9 (.D(RAM_Out_1), .en(en9), .Q(_1_9), .clk(clk), .clr(reset));
  Register #(.width(32)) C1_10 (.D(RAM_Out_1), .en(en10), .Q(_1_10), .clk(clk), .clr(reset));
  Register #(.width(32)) C1_11 (.D(RAM_Out_1), .en(en11), .Q(_1_11), .clk(clk), .clr(reset));
  Register #(.width(32)) C1_12 (.D(RAM_Out_1), .en(en12), .Q(_1_12), .clk(clk), .clr(reset));
  Register #(.width(32)) C1_13 (.D(RAM_Out_1), .en(en13), .Q(_1_13), .clk(clk), .clr(reset));
  Register #(.width(32)) C1_14 (.D(RAM_Out_1), .en(en14), .Q(_1_14), .clk(clk), .clr(reset));
  Register #(.width(32)) C1_15 (.D(RAM_Out_1), .en(en15), .Q(_1_15), .clk(clk), .clr(reset));
  Register #(.width(32)) C2_0 (.D(RAM_Out_2), .en(en0), .Q(_2_0), .clk(clk), .clr(reset));
  Register #(.width(32)) C2_1 (.D(RAM_Out_2), .en(en1), .Q(_2_1), .clk(clk), .clr(reset));
  Register #(.width(32)) C2_2 (.D(RAM_Out_2), .en(en2), .Q(_2_2), .clk(clk), .clr(reset));
  Register #(.width(32)) C2_3 (.D(RAM_Out_2), .en(en3), .Q(_2_3), .clk(clk), .clr(reset));
  Register #(.width(32)) C2_4 (.D(RAM_Out_2), .en(en4), .Q(_2_4), .clk(clk), .clr(reset));
  Register #(.width(32)) C2_5 (.D(RAM_Out_2), .en(en5), .Q(_2_5), .clk(clk), .clr(reset));
  Register #(.width(32)) C2_6 (.D(RAM_Out_2), .en(en6), .Q(_2_6), .clk(clk), .clr(reset));
  Register #(.width(32)) C2_7 (.D(RAM_Out_2), .en(en7), .Q(_2_7), .clk(clk), .clr(reset));
  Register #(.width(32)) C2_8 (.D(RAM_Out_2), .en(en8), .Q(_2_8), .clk(clk), .clr(reset));
  Register #(.width(32)) C2_9 (.D(RAM_Out_2), .en(en9), .Q(_2_9), .clk(clk), .clr(reset));
  Register #(.width(32)) C2_10 (.D(RAM_Out_2), .en(en10), .Q(_2_10), .clk(clk), .clr(reset));
  Register #(.width(32)) C2_11 (.D(RAM_Out_2), .en(en11), .Q(_2_11), .clk(clk), .clr(reset));
  Register #(.width(32)) C2_12 (.D(RAM_Out_2), .en(en12), .Q(_2_12), .clk(clk), .clr(reset));
  Register #(.width(32)) C2_13 (.D(RAM_Out_2), .en(en13), .Q(_2_13), .clk(clk), .clr(reset));
  Register #(.width(32)) C2_14 (.D(RAM_Out_2), .en(en14), .Q(_2_14), .clk(clk), .clr(reset));
  Register #(.width(32)) C2_15 (.D(RAM_Out_2), .en(en15), .Q(_2_15), .clk(clk), .clr(reset));
  Register #(.width(32)) C3_0 (.D(RAM_Out_3), .en(en0), .Q(_3_0), .clk(clk), .clr(reset));
  Register #(.width(32)) C3_1 (.D(RAM_Out_3), .en(en1), .Q(_3_1), .clk(clk), .clr(reset));
  Register #(.width(32)) C3_2 (.D(RAM_Out_3), .en(en2), .Q(_3_2), .clk(clk), .clr(reset));
  Register #(.width(32)) C3_3 (.D(RAM_Out_3), .en(en3), .Q(_3_3), .clk(clk), .clr(reset));
  Register #(.width(32)) C3_4 (.D(RAM_Out_3), .en(en4), .Q(_3_4), .clk(clk), .clr(reset));
  Register #(.width(32)) C3_5 (.D(RAM_Out_3), .en(en5), .Q(_3_5), .clk(clk), .clr(reset));
  Register #(.width(32)) C3_6 (.D(RAM_Out_3), .en(en6), .Q(_3_6), .clk(clk), .clr(reset));
  Register #(.width(32)) C3_7 (.D(RAM_Out_3), .en(en7), .Q(_3_7), .clk(clk), .clr(reset));
  Register #(.width(32)) C3_8 (.D(RAM_Out_3), .en(en8), .Q(_3_8), .clk(clk), .clr(reset));
  Register #(.width(32)) C3_9 (.D(RAM_Out_3), .en(en9), .Q(_3_9), .clk(clk), .clr(reset));
  Register #(.width(32)) C3_10 (.D(RAM_Out_3), .en(en10), .Q(_3_10), .clk(clk), .clr(reset));
  Register #(.width(32)) C3_11 (.D(RAM_Out_3), .en(en11), .Q(_3_11), .clk(clk), .clr(reset));
  Register #(.width(32)) C3_12 (.D(RAM_Out_3), .en(en12), .Q(_3_12), .clk(clk), .clr(reset));
  Register #(.width(32)) C3_13 (.D(RAM_Out_3), .en(en13), .Q(_3_13), .clk(clk), .clr(reset));
  Register #(.width(32)) C3_14 (.D(RAM_Out_3), .en(en14), .Q(_3_14), .clk(clk), .clr(reset));
  Register #(.width(32)) C3_15 (.D(RAM_Out_3), .en(en15), .Q(_3_15), .clk(clk), .clr(reset));

  // Other names for the same wires on the sheet: index[3:0] = Address[3:0]; Tag[11:0] = Address[15:4]
endmodule
