// Logisim project Control Unit.circ as structural Verilog: 3 circuits, main circuit Control Unit
module Control_Unit (
  input  clk,
  input  Reset,
  input  [3:0] RT,
  input  [3:0] WT,
  input  [2:0] OP_Sel,
  input  Is_On_Cache,
  output Data_ready,
  output Inst_ready,
  output PC_load,
  output GetInst,
  output Load_SP,
  output tty_enable,
  output kbd_enable,
  output Invalidate_cache_address,
  output stop,
  output CS,
  output nRW,
  output EN_RF,
  output KBD_CLR
);

  wire and_1_out, and_2_out, cn, comparator_1_eq, CS1, CS2, CS3, CS5, demultiplexer_1_out0,
       demultiplexer_1_out1, demultiplexer_1_out3, demultiplexer_1_out4, demultiplexer_2_out0,
       demultiplexer_2_out1, demultiplexer_4_out1, END_q, Halt_q, IDLE_q, not_1_out, nRW_2, or_4_out,
       or_5_out, or_6_out, or_7_out, or_9_out, Wait_PC_load_2_q;
  wire [3:0] counter_1_q;

  or or_1 (CS, CS1, CS2, CS3, GetInst, Inst_ready, CS5, Data_ready);
  or or_2 (nRW, CS1, Inst_ready, nRW_2);
  or or_3 (EN_RF, GetInst, Data_ready, CS5);
  D_Flip_Flop #(.trigger("falling")) Wait_PC_load (
    .clk(clk), .D(cn), .Q(GetInst), .reset(Reset));  // open: Qn, preset, en
  D_Flip_Flop #(.trigger("falling")) END (.clk(clk), .D(GetInst), .Q(END_q), .reset(Reset));  // open: Qn, preset, en
  D_Flip_Flop #(.trigger("falling")) Wait_PC_load_2 (
    .clk(clk), .D(Inst_ready), .Q(Wait_PC_load_2_q), .reset(Reset));  // open: Qn, preset, en
  Demultiplexer #(.select(3), .enable("false")) demultiplexer_1 (
    .out0(demultiplexer_1_out0), .out1(demultiplexer_1_out1), .out2(Load_SP), .out3(demultiplexer_1_out3),
    .out4(demultiplexer_1_out4), .out6(kbd_enable), .in(Wait_PC_load_2_q), .sel(OP_Sel));  // open: out5, out7
  or or_4 (or_4_out, demultiplexer_2_out0, END_q);
  D_Flip_Flop #(.trigger("falling")) IDLE (.clk(clk), .D(or_4_out), .Q(IDLE_q), .preset(Reset));  // open: Qn, en, reset
  Demultiplexer #(.enable("false")) demultiplexer_2 (
    .out0(demultiplexer_2_out0), .out1(demultiplexer_2_out1), .in(IDLE_q), .sel(not_1_out));
  not not_1 (not_1_out, Reset);
  or or_5 (or_5_out, and_2_out, demultiplexer_2_out1);
  Waiter_R waiter_r_1 (
    .start(demultiplexer_1_out1), .clk(clk), .RT(RT), .Cached(Is_On_Cache), .CS(CS2), .ready(Data_ready));
  Waiter_W waiter_w_1 (
    .in_1(clk), .start(Load_SP), .WT(WT), .CS(CS3), .ready(CS5),
    .Invalidate_cache_address(Invalidate_cache_address));
  or or_6 (or_6_out, demultiplexer_1_out4, stop);
  D_Flip_Flop #(.trigger("falling")) Read_Inst (
    .clk(clk), .D(or_5_out), .Q(nRW_2), .reset(Reset));  // open: Qn, preset, en
  Demultiplexer #(.enable("false")) demultiplexer_3 (.out0(stop), .in(Halt_q), .sel(Reset));  // open: out1
  D_Flip_Flop #(.trigger("falling")) Halt (.clk(clk), .D(or_6_out), .Q(Halt_q));  // open: Qn, preset, en, reset
  Demultiplexer #(.enable("false")) demultiplexer_4 (
    .out0(CS1), .out1(demultiplexer_4_out1), .in(nRW_2), .sel(and_1_out));
  and and_1 (and_1_out, nRW_2, Is_On_Cache);
  and and_2 (and_2_out, ~comparator_1_eq, CS1);  // AND_Gate
  Counter #(.width(4), .max('hf)) counter_1 (
    .count(CS1), .Q(counter_1_q), .clk(clk), .clr(or_7_out));  // open: load, D, carry
  or or_7 (or_7_out, Inst_ready, Reset);
  D_Flip_Flop #(.trigger("falling")) Wait_PC_load_3 (
    .clk(clk), .D(demultiplexer_1_out3), .Q(tty_enable), .reset(Reset));  // open: Qn, preset, en
  Comparator #(.width(4)) comparator_1 (.a(RT), .b(counter_1_q), .eq(comparator_1_eq));  // open: gt, lt
  or or_8 (cn, demultiplexer_1_out0, Data_ready, CS5, tty_enable, kbd_enable);
  or or_9 (or_9_out, demultiplexer_4_out1, comparator_1_eq);
  D_Flip_Flop #(.trigger("falling")) d_ff_1 (
    .clk(clk), .D(or_9_out), .Q(Inst_ready), .reset(Reset));  // open: Qn, preset, en

  assign KBD_CLR = Reset;
  assign PC_load = GetInst;

  // Other names for the same wires on the sheet: nRW_t = CS1; CS4 = Inst_ready; nRW_1 = Inst_ready; CS7 = GetInst;
  //   LR_1 = GetInst; CS6 = Data_ready; LR_2 = Data_ready; LR_3 = CS5
endmodule

module Waiter_R (
  input  start,
  input  clk,
  input  [3:0] RT,
  input  Cached,
  output CS,
  output ready
);

  wire and_1_out, and_2_out, comparator_1_eq, demultiplexer_1_out0, or_1_out, or_2_out, or_3_out, Read_Inst_q;
  wire [3:0] counter_1_q;

  and and_1 (and_1_out, ~comparator_1_eq, demultiplexer_1_out0);  // AND_Gate
  or or_1 (or_1_out, and_1_out, start);
  D_Flip_Flop #(.trigger("falling")) Read_Inst (
    .clk(clk), .D(or_1_out), .Q(Read_Inst_q));  // open: Qn, preset, en, reset
  Demultiplexer #(.enable("false")) demultiplexer_1 (
    .out0(demultiplexer_1_out0), .out1(CS), .in(Read_Inst_q), .sel(and_2_out));
  and and_2 (and_2_out, Read_Inst_q, Cached);
  Counter #(.width(4), .max('hf)) counter_1 (
    .count(demultiplexer_1_out0), .Q(counter_1_q), .clk(clk), .clr(or_2_out));  // open: load, D, carry
  or or_2 (or_2_out, ready, start);
  or or_3 (or_3_out, CS, comparator_1_eq);
  Comparator #(.width(4)) comparator_1 (.a(RT), .b(counter_1_q), .eq(comparator_1_eq));  // open: gt, lt
  D_Flip_Flop #(.trigger("falling")) d_ff_1 (.clk(clk), .D(or_3_out), .Q(ready));  // open: Qn, preset, en, reset
endmodule

module Waiter_W (
  input  in_1,
  input  start,
  input  [3:0] WT,
  output CS,
  output ready,
  output Invalidate_cache_address
);

  wire and_1_out, comparator_1_eq, or_1_out, or_2_out;
  wire [3:0] counter_1_q;

  and and_1 (and_1_out, ~comparator_1_eq, CS);  // AND_Gate
  or or_1 (or_1_out, and_1_out, start);
  D_Flip_Flop #(.trigger("falling")) Read_Inst (.clk(in_1), .D(or_1_out), .Q(CS));  // open: Qn, preset, en, reset
  Counter #(.width(4), .max('hf)) counter_1 (
    .count(CS), .Q(counter_1_q), .clk(in_1), .clr(or_2_out));  // open: load, D, carry
  or or_2 (or_2_out, ready, start);
  Comparator #(.width(4)) comparator_1 (.a(WT), .b(counter_1_q), .eq(comparator_1_eq));  // open: gt, lt
  D_Flip_Flop #(.trigger("falling")) d_ff_1 (
    .clk(in_1), .D(comparator_1_eq), .Q(ready));  // open: Qn, preset, en, reset

  assign Invalidate_cache_address = CS;

  // Other names for the same wires on the sheet: clk = in_1
endmodule
