// Logisim project Data Path.circ as structural Verilog: 1 circuit, main circuit Data Path
module Data_Path (
  input  CLEAR,
  input  CLOCK,
  input  [31:0] INSTRUCTION,
  input  [6:0] KEYBOARD,
  input  KBD_AVAIL,
  input  EN_PC,
  input  LOAD_INST,
  input  EN_RF,
  input  nRW,
  input  Lsp,
  input  GET_INST,
  output [31:0] RAM_INPUT,
  output [1:0] RAM_BANK_SEL,
  output [15:0] RAM_ADDRESS,
  output R___W,
  output [3:0] MASK,
  output [6:0] TTY_DATA,
  output [2:0] Op_code
);

  wire and_2_out, EN_HL, HALT, I_LOGIC, KBD, LW, N, or_1_out, or_3_out, or_4_out, or_5_out, or_6_out, POP,
       PUSH, RF_WRITE, RND, SW, TTY, TYPE_I, Z;
  wire [1:0] MFHI___MFLO, priority_encoder_1_out;
  wire [3:0] ALU_SEL;
  wire [4:0] multiplexer_5_out, Rd, Rs, Rt;
  wire [7:0] BC_op_code;
  wire [15:0] K;
  wire [25:0] DESTINO_SALTO;
  wire [31:0] ALU_OUTPUT, B, BC_OUT, bit_extender_1_out, bit_extender_2_out, bit_extender_3_out,
       bit_extender_4_out, HI, KEYBOARD_t, multiplexer_2_out, multiplexer_3_out, multiplexer_4_out,
       multiplexer_6_out, multiplexer_7_out, PC, random_1_out, register_1_q, SP;
  wire [31:7] A;

  Multiplexer #(.width(32), .enable("false")) multiplexer_1 (
    .in0({A, TTY_DATA}), .in1(B), .out(RAM_INPUT), .sel(or_1_out));
  or or_1 (or_1_out, SW, PUSH);
  or or_2 (R___W, PUSH, SW);
  Program_Counter program_counter_1 (
    .CLK(CLOCK), .RESET(CLEAR), .ENABLE(EN_PC), .PC_new_value(BC_OUT), .PC_current_value(PC));
  Branch_Control branch_control_1 (
    .DEST(DESTINO_SALTO), .PC(PC), .Rs({A, TTY_DATA}), .Rt(B), .OFFSET(K), .Op_code(BC_op_code),
    .BC_OUT(BC_OUT));
  Register #(.width(32)) register_1 (.D(INSTRUCTION), .en(LOAD_INST), .Q(register_1_q), .clk(CLOCK), .clr(CLEAR));
  INSTRUCTION_DECODER instruction_decoder_1 (
    .Instruction(register_1_q), .K(K), .Destino_Salto(DESTINO_SALTO), .Rt(Rt), .Rs(Rs), .Rd(Rd), .SW(SW),
    .POP(POP), .PUSH(PUSH), .HALT(HALT), .RND(RND), .TTY(TTY), .KBD(KBD), .ALU_SEL(ALU_SEL), .TYPE_I(TYPE_I),
    .EN_H_L(EN_HL), .MFHI___MFLO(MFHI___MFLO), .BC_op_code(BC_op_code), .RF_WRITE(RF_WRITE),
    .I_LOGIC(I_LOGIC), .LW(LW));
  Random #(.width(32)) random_1 (.clk(CLOCK), .next(RND), .out(random_1_out));  // open: clr
  assign bit_extender_1_out = {{25{1'b0}}, KEYBOARD};  // Bit_Extender bit_extender_1
  assign KEYBOARD_t = bit_extender_1_out & bit_extender_2_out;  // AND_Gate and_1, 32 bits wide
  assign bit_extender_2_out = {{31{KBD_AVAIL}}, KBD_AVAIL};  // Bit_Extender bit_extender_2
  Multiplexer #(.width(32), .enable("false")) multiplexer_2 (
    .in0(ALU_OUTPUT), .in1({A, TTY_DATA}), .out(multiplexer_2_out), .sel(or_3_out));
  or or_3 (or_3_out, POP, PUSH);
  Multiplexer #(.select(2), .width(32), .enable("false")) multiplexer_3 (
    .in0(ALU_OUTPUT), .in1(KEYBOARD_t), .in2(random_1_out), .out(multiplexer_3_out),
    .sel(priority_encoder_1_out));  // open: in3
  Priority_Encoder #(.select(2)) priority_encoder_1 (
    .in0(1'b1), .in1(KBD), .in2(RND), .out(priority_encoder_1_out));  // open: in3, gs, en_out, en_in
  Multiplexer #(.width(32), .enable("false")) multiplexer_4 (
    .in0(PC), .in1(multiplexer_2_out),
    .out({multiplexer_4_out[31:20], RAM_ADDRESS, RAM_BANK_SEL, multiplexer_4_out[1:0]}), .sel(and_2_out));
  and and_2 (and_2_out, or_4_out, ~nRW);  // AND_Gate
  or or_4 (or_4_out, SW, LW, POP, PUSH);
  Multiplexer #(.width(5), .enable("false")) multiplexer_5 (.in0(Rd), .in1(Rt), .out(multiplexer_5_out), .sel(TYPE_I));
  // Register_File register_file_1: pin names not known; wires that end beside it: multiplexer_5_out, multiplexer_3_out, HI, EN_RF, MFHI___MFLO, EN_HL, POP, PUSH, Lsp, GET_INST, CLOCK, CLEAR, Rs, Rt, {A, TTY_DATA}, B, SP
  assign bit_extender_3_out = {{16{K[15]}}, K};  // Bit_Extender bit_extender_3
  Multiplexer #(.width(32), .enable("false")) multiplexer_6 (
    .in0(bit_extender_3_out), .in1(bit_extender_4_out), .out(multiplexer_6_out), .sel(I_LOGIC));
  assign bit_extender_4_out = {{16{1'b0}}, K};  // Bit_Extender bit_extender_4
  and and_3 (MASK[0], ~RAM_BANK_SEL[0], ~RAM_BANK_SEL[1]);  // AND_Gate
  and and_4 (MASK[1], RAM_BANK_SEL[0], ~RAM_BANK_SEL[1]);  // AND_Gate
  and and_5 (MASK[2], ~RAM_BANK_SEL[0], RAM_BANK_SEL[1]);  // AND_Gate
  and and_6 (MASK[3], RAM_BANK_SEL[0], RAM_BANK_SEL[1]);
  Multiplexer #(.width(32), .enable("false")) multiplexer_7 (
    .in0(B), .in1(multiplexer_6_out), .out(multiplexer_7_out), .sel(TYPE_I));
  or or_5 (or_5_out, POP, LW);
  or or_6 (or_6_out, PUSH, SW);
  ALU alu_1 (.A({A, TTY_DATA}), .B(multiplexer_7_out), .Sel(ALU_SEL), .HI(HI), .Out___LO(ALU_OUTPUT), .Z(Z), .N(N));
  Priority_Encoder priority_encoder_2 (
    .in0(1'b1), .in1(or_5_out), .in2(or_6_out), .in3(TTY), .in4(HALT), .in5(KBD), .out(Op_code));  // open: in6, in7, en_in, gs, en_out

  // Other names for the same wires on the sheet: A[6:0] = TTY_DATA; CLK = CLOCK; CLR = CLEAR; IN_KBD[6:0] = KEYBOARD;
  //   LD_INST = LOAD_INST

  // Notes on the sheet:
  //   DATA PATH
endmodule
