// Logisim project Instruction Decoder.circ as structural Verilog: 1 circuit, main circuit INSTRUCTION DECODER
module INSTRUCTION_DECODER (
  input  [31:0] Instruction,
  output LW,
  output [15:0] K,
  output SW,
  output POP,
  output PUSH,
  output [25:0] Destino_Salto,
  output HALT,
  output TTY,
  output [4:0] Rt,
  output RND,
  output [4:0] Rs,
  output KBD,
  output [4:0] Rd,
  output [3:0] ALU_SEL,
  output TYPE_I,
  output I_LOGIC,
  output [1:0] MFHI___MFLO,
  output EN_H_L,
  output [7:0] BC_op_code,
  output RF_WRITE
);

  wire _00, _3f, _38, ADD, ADD_, ADDI, AND, AND_, ANDI, comparator_4_eq, comparator_5_eq, comparator_6_eq,
       comparator_7_eq, comparator_8_eq, comparator_14_eq, comparator_15_eq, comparator_16_eq,
       comparator_17_eq, comparator_18_eq, comparator_25_eq, comparator_26_eq, comparator_27_eq,
       comparator_28_eq, comparator_31_eq, comparator_32_eq, comparator_33_eq, comparator_34_eq,
       comparator_36_eq, comparator_37_eq, comparator_38_eq, comparator_39_eq, DIV, DIVU, MULT, MULU, NOR,
       OR, OR_, ORI, SLT, SLT_, SLTI, SLTIU, SLTU, SLTU_, SUB, XOR, XOR_, XORI;
  wire [5:0] Func_Code, OP_Code;

  Comparator #(.width(6)) comparator_1 (.a(OP_Code), .b({6{1'b0}}), .eq(_00));  // open: gt, lt
  Comparator #(.width(6)) comparator_2 (.a(OP_Code), .b(6'b111000), .eq(_38));  // open: gt, lt
  Comparator #(.width(6)) comparator_3 (.a(OP_Code), .b({6{1'b1}}), .eq(_3f));  // open: gt, lt
  and and_1 (ADD, _00, comparator_4_eq);
  Comparator #(.width(6)) comparator_4 (.a(Func_Code), .b(6'b100000), .eq(comparator_4_eq));  // open: gt, lt
  and and_2 (AND, _00, comparator_5_eq);
  Comparator #(.width(6)) comparator_5 (.a(Func_Code), .b(6'b100100), .eq(comparator_5_eq));  // open: gt, lt
  and and_3 (BC_op_code[0], _00, comparator_6_eq);
  Comparator #(.width(6)) comparator_6 (.a(Func_Code), .b({6{1'b0}}), .eq(comparator_6_eq));  // open: gt, lt
  and and_4 (POP, _38, comparator_7_eq);
  Comparator #(.width(6)) comparator_7 (.a(Func_Code), .b({6{1'b0}}), .eq(comparator_7_eq));  // open: gt, lt
  and and_5 (TTY, _3f, comparator_8_eq);
  Comparator #(.width(6)) comparator_8 (.a(Func_Code), .b(6'b000001), .eq(comparator_8_eq));  // open: gt, lt
  Comparator #(.width(6)) comparator_9 (.a(OP_Code), .b(6'b000001), .eq(BC_op_code[5]));  // open: gt, lt
  Comparator #(.width(6)) comparator_10 (.a(OP_Code), .b(6'b000100), .eq(BC_op_code[1]));  // open: gt, lt
  Comparator #(.width(6)) comparator_11 (.a(OP_Code), .b(6'b000101), .eq(BC_op_code[2]));  // open: gt, lt
  Comparator #(.width(6)) comparator_12 (.a(OP_Code), .b(6'b000110), .eq(BC_op_code[3]));  // open: gt, lt
  Comparator #(.width(6)) comparator_13 (.a(OP_Code), .b(6'b000111), .eq(BC_op_code[4]));  // open: gt, lt
  and and_6 (SUB, _00, comparator_14_eq);
  Comparator #(.width(6)) comparator_14 (.a(Func_Code), .b(6'b100010), .eq(comparator_14_eq));  // open: gt, lt
  and and_7 (OR, _00, comparator_15_eq);
  Comparator #(.width(6)) comparator_15 (.a(Func_Code), .b(6'b100101), .eq(comparator_15_eq));  // open: gt, lt
  and and_8 (BC_op_code[7], _00, comparator_16_eq);
  Comparator #(.width(6)) comparator_16 (.a(Func_Code), .b(6'b001000), .eq(comparator_16_eq));  // open: gt, lt
  and and_9 (PUSH, _38, comparator_17_eq);
  Comparator #(.width(6)) comparator_17 (.a(Func_Code), .b(6'b000001), .eq(comparator_17_eq));  // open: gt, lt
  and and_10 (RND, _3f, comparator_18_eq);
  Comparator #(.width(6)) comparator_18 (.a(Func_Code), .b(6'b000010), .eq(comparator_18_eq));  // open: gt, lt
  Comparator #(.width(6)) comparator_19 (.a(OP_Code), .b(6'b001000), .eq(ADDI));  // open: gt, lt
  Comparator #(.width(6)) comparator_20 (.a(OP_Code), .b(6'b001010), .eq(SLTI));  // open: gt, lt
  Comparator #(.width(6)) comparator_21 (.a(OP_Code), .b(6'b001011), .eq(SLTIU));  // open: gt, lt
  Comparator #(.width(6)) comparator_22 (.a(OP_Code), .b(6'b001100), .eq(ANDI));  // open: gt, lt
  Comparator #(.width(6)) comparator_23 (.a(OP_Code), .b(6'b001101), .eq(ORI));  // open: gt, lt
  Comparator #(.width(6)) comparator_24 (.a(OP_Code), .b(6'b001110), .eq(XORI));  // open: gt, lt
  and and_11 (MULT, _00, comparator_25_eq);
  Comparator #(.width(6)) comparator_25 (.a(Func_Code), .b(6'b011000), .eq(comparator_25_eq));  // open: gt, lt
  and and_12 (NOR, _00, comparator_26_eq);
  Comparator #(.width(6)) comparator_26 (.a(Func_Code), .b(6'b100110), .eq(comparator_26_eq));  // open: gt, lt
  and and_13 (MFHI___MFLO[0], _00, comparator_27_eq);
  Comparator #(.width(6)) comparator_27 (.a(Func_Code), .b(6'b010000), .eq(comparator_27_eq));  // open: gt, lt
  and and_14 (KBD, _3f, comparator_28_eq);
  Comparator #(.width(6)) comparator_28 (.a(Func_Code), .b(6'b000100), .eq(comparator_28_eq));  // open: gt, lt
  Comparator #(.width(6)) comparator_29 (.a(OP_Code), .b(6'b100011), .eq(LW));  // open: gt, lt
  Comparator #(.width(6)) comparator_30 (.a(OP_Code), .b(6'b101011), .eq(SW));  // open: gt, lt
  Comparator #(.width(6)) comparator_31 (.a(Func_Code), .b(6'b011001), .eq(comparator_31_eq));  // open: gt, lt
  Comparator #(.width(6)) comparator_32 (.a(Func_Code), .b(6'b100111), .eq(comparator_32_eq));  // open: gt, lt
  Comparator #(.width(6)) comparator_33 (.a(Func_Code), .b(6'b010001), .eq(comparator_33_eq));  // open: gt, lt
  Comparator #(.width(6)) comparator_34 (.a(Func_Code), .b({6{1'b1}}), .eq(comparator_34_eq));  // open: gt, lt
  or or_1 (TYPE_I, ADDI, ANDI, ORI, XORI, SLTI, SLTIU, LW, SW);
  or or_2 (EN_H_L, MULT, MULU, DIV, DIVU);
  or or_3 (ADD_, ADD, ADDI, LW, SW);
  or or_4 (AND_, AND, ANDI);
  or or_5 (OR_, OR, ORI);
  or or_6 (XOR_, XOR, XORI);
  or or_7 (SLT_, SLT, SLTI);
  or or_8 (SLTU_, SLTU, SLTIU);
  and and_15 (MULU, _00, comparator_31_eq);
  and and_16 (XOR, _00, comparator_32_eq);
  and and_17 (MFHI___MFLO[1], _00, comparator_33_eq);
  and and_18 (HALT, _3f, comparator_34_eq);
  Comparator #(.width(6)) comparator_35 (.a(OP_Code), .b(6'b000010), .eq(BC_op_code[6]));  // open: gt, lt
  Comparator #(.width(6)) comparator_36 (.a(Func_Code), .b(6'b011010), .eq(comparator_36_eq));  // open: gt, lt
  Comparator #(.width(6)) comparator_37 (.a(Func_Code), .b(6'b101010), .eq(comparator_37_eq));  // open: gt, lt
  or or_9 (I_LOGIC, ANDI, ORI, XORI);
  and and_19 (DIV, _00, comparator_36_eq);
  and and_20 (SLT, _00, comparator_37_eq);
  or or_10 (RF_WRITE, ADD, ADDI, LW, SUB, AND_, OR_, XOR_, NOR, SLT_, SLTU_, MFHI___MFLO[0], MFHI___MFLO[1], RND, KBD);
  Priority_Encoder #(.select(4)) priority_encoder_1 (
    .in0(AND_), .in1(OR_), .in2(NOR), .in3(XOR_), .in4(SLT_), .in5(SLTU_), .in6(ADD_), .in7(SUB), .in8(MULT),
    .in9(MULU), .in10(DIV), .in11(DIVU), .out(ALU_SEL));  // open: in12, in13, in14, in15, gs, en_out, en_in
  Comparator #(.width(6)) comparator_38 (.a(Func_Code), .b(6'b011011), .eq(comparator_38_eq));  // open: gt, lt
  Comparator #(.width(6)) comparator_39 (.a(Func_Code), .b(6'b101011), .eq(comparator_39_eq));  // open: gt, lt
  and and_21 (DIVU, _00, comparator_38_eq);
  and and_22 (SLTU, _00, comparator_39_eq);

  assign Destino_Salto = {Instruction[1:0], Instruction[15:8], Instruction[23:16], Instruction[31:24]};
  assign K = {Instruction[23:16], Instruction[31:24]};
  assign Rd = Instruction[23:19];
  assign Rs = {Instruction[1:0], Instruction[15:13]};
  assign Rt = Instruction[12:8];

  // Other names for the same wires on the sheet: Func_Code_t[5:0] = Instruction[29:24];
  //   OP_Code_t[5:0] = Instruction[7:2]; NOP = BC_op_code[0]; BEQ = BC_op_code[1]; BNE = BC_op_code[2];
  //   BLEZ = BC_op_code[3]; BGTZ = BC_op_code[4]; BLTZ = BC_op_code[5]; J = BC_op_code[6]; JR = BC_op_code[7];
  //   MFHI = MFHI___MFLO[0]; MFLO = MFHI___MFLO[1]

  // Notes on the sheet:
  //   OUTPUT
  //   Instrucciones Tipo R
  //   INSTRUCTION DECODER
  //   Instrucciones Tipo I
  //   Instrucciones Tipo R
  //   Instrucciones Tipo J
endmodule
