// Logisim project Memory Address.circ as structural Verilog: 1 circuit, main circuit Memory Address
module Memory_Address (
  input  POP,
  input  PUSH,
  input  [31:0] ALU,
  input  [31:0] PC,
  input  [31:0] SP,
  input  LW,
  input  SW,
  input  PC_ADDRESS,
  output [31:0] MEMORY
);

  wire [1:0] or_2_out;
  wire [31:0] multiplexer_1_out, subtractor_1_out;

  Subtractor #(.width(32)) subtractor_1 (.a(SP), .b(32'h4), .out(subtractor_1_out));  // open: bin, bout
  Multiplexer #(.width(32), .enable("false")) multiplexer_1 (
    .in0(SP), .in1(subtractor_1_out), .out(multiplexer_1_out), .sel(PUSH));
  Multiplexer #(.select(2), .width(32), .enable("false")) multiplexer_2 (
    .in0(PC), .in1(ALU), .in2(multiplexer_1_out), .in3(PC), .out(MEMORY), .sel(or_2_out));
  or or_1 (or_2_out[1], PUSH, POP, PC_ADDRESS);
  or or_2 (or_2_out[0], PC_ADDRESS, LW, SW);

  // Notes on the sheet:
  //   Memory_Address
endmodule
