// Logisim project Program Counter.circ as structural Verilog: 1 circuit, main circuit Program Counter
module Program_Counter (
  input  CLK,
  input  RESET,
  input  ENABLE,
  input  [31:0] PC_new_value,
  output [31:0] PC_current_value
);

  Register #(.width(32)) PC (.D(PC_new_value), .en(ENABLE), .Q(PC_current_value), .clk(CLK), .clr(RESET));

  // Notes on the sheet:
  //   PROGRAM COUNTER
endmodule
