// Logisim project Register File.circ as structural Verilog: 1 circuit, main circuit Register File
module Register_File (
  input  Clock,
  input  Reset,
  input  [31:0] Input,
  input  [4:0] SEL_Rs,
  input  [4:0] SEL_Rt,
  input  [4:0] DA,
  input  Load_Registers,
  input  Enable_H_L,
  input  [1:0] MFHI___MFLO,
  input  [31:0] HI_in,
  input  POP,
  input  Push,
  input  Lsp,
  input  GET_INST,
  output [31:0] Rs,
  output [31:0] Rt
);

  wire and_2_out, and_3_out, EN_SP, R01, R02, R03, R04, R05, R06, R07, R08, R09, R10, R11, R12, R13, R14,
       R15, R16, R17, R18, R19, R20, R21, R22, R23, R24, R25, R26, R27, R28, R29, R30, R31;
  wire [4:0] and_1_out, bit_extender_1_out;
  wire [31:0] D00, D01, D02, D03, D04, D05, D06, D07, D08, D09, D10, D11, D12, D13, D14, D15, D16, D17, D18,
       D19, D20, D21, D22, D23, D24, D25, D26, D27, D28, D29, D30, D31, HI, IN, LO;

  Register #(.width(32)) register_1 (.D(IN), .en(1'b0), .Q(D00), .clk(Clock), .clr(Reset));
  Register #(.width(32)) register_2 (.D(IN), .en(R01), .Q(D01), .clk(Clock), .clr(Reset));
  Register #(.width(32)) register_3 (.D(IN), .en(R02), .Q(D02), .clk(Clock), .clr(Reset));
  Register #(.width(32)) register_4 (.D(IN), .en(R03), .Q(D03), .clk(Clock), .clr(Reset));
  Register #(.width(32)) register_5 (.D(IN), .en(R04), .Q(D04), .clk(Clock), .clr(Reset));
  Register #(.width(32)) register_6 (.D(IN), .en(R05), .Q(D05), .clk(Clock), .clr(Reset));
  Register #(.width(32)) register_7 (.D(IN), .en(R06), .Q(D06), .clk(Clock), .clr(Reset));
  Register #(.width(32)) register_8 (.D(IN), .en(R07), .Q(D07), .clk(Clock), .clr(Reset));
  Register #(.width(32)) register_9 (.D(IN), .en(R08), .Q(D08), .clk(Clock), .clr(Reset));
  Register #(.width(32)) register_10 (.D(IN), .en(R09), .Q(D09), .clk(Clock), .clr(Reset));
  Register #(.width(32)) register_11 (.D(IN), .en(R10), .Q(D10), .clk(Clock), .clr(Reset));
  Register #(.width(32)) register_12 (.D(IN), .en(R11), .Q(D11), .clk(Clock), .clr(Reset));
  Register #(.width(32)) register_13 (.D(IN), .en(R12), .Q(D12), .clk(Clock), .clr(Reset));
  Register #(.width(32)) register_14 (.D(IN), .en(R13), .Q(D13), .clk(Clock), .clr(Reset));
  Register #(.width(32)) register_15 (.D(IN), .en(R14), .Q(D14), .clk(Clock), .clr(Reset));
  Register #(.width(32)) register_16 (.D(IN), .en(R15), .Q(D15), .clk(Clock), .clr(Reset));
  Register #(.width(32)) u_HI (.D(HI_in), .en(Enable_H_L), .Q(HI), .clk(Clock), .clr(Reset));
  Register #(.width(32)) register_17 (.D(IN), .en(R16), .Q(D16), .clk(Clock), .clr(Reset));
  Register #(.width(32)) register_18 (.D(IN), .en(R17), .Q(D17), .clk(Clock), .clr(Reset));
  Register #(.width(32)) register_19 (.D(IN), .en(R18), .Q(D18), .clk(Clock), .clr(Reset));
  Register #(.width(32)) register_20 (.D(IN), .en(R19), .Q(D19), .clk(Clock), .clr(Reset));
  Register #(.width(32)) register_21 (.D(IN), .en(R20), .Q(D20), .clk(Clock), .clr(Reset));
  Register #(.width(32)) register_22 (.D(IN), .en(R21), .Q(D21), .clk(Clock), .clr(Reset));
  Register #(.width(32)) register_23 (.D(IN), .en(R22), .Q(D22), .clk(Clock), .clr(Reset));
  Register #(.width(32)) register_24 (.D(IN), .en(R23), .Q(D23), .clk(Clock), .clr(Reset));
  Register #(.width(32)) u_LO (.D(Input), .en(Enable_H_L), .Q(LO), .clk(Clock), .clr(Reset));
  Demultiplexer #(.select(5), .enable("false")) demultiplexer_1 (
    .out1(R01), .out2(R02), .out3(R03), .out4(R04), .out5(R05), .out6(R06), .out7(R07), .out8(R08),
    .out9(R09), .out10(R10), .out11(R11), .out12(R12), .out13(R13), .out14(R14), .out15(R15), .out16(R16),
    .out17(R17), .out18(R18), .out19(R19), .out20(R20), .out21(R21), .out22(R22), .out23(R23), .out24(R24),
    .out25(R25), .out26(R26), .out27(R27), .out28(R28), .out29(R29), .out30(R30), .out31(R31), .in(1'b1),
    .sel(and_1_out));  // open: out0
  assign and_1_out = bit_extender_1_out & DA;  // AND_Gate and_1, 5 bits wide
  assign bit_extender_1_out = {{4{Load_Registers}}, Load_Registers};  // Bit_Extender bit_extender_1
  Multiplexer #(.select(2), .width(32), .enable("false")) multiplexer_1 (
    .in0(Input), .in1(HI), .in2(LO), .out(IN), .sel(MFHI___MFLO));  // open: in3
  Register #(.width(32)) register_25 (.D(IN), .en(R24), .Q(D24), .clk(Clock), .clr(Reset));
  Register #(.width(32)) register_26 (.D(IN), .en(R25), .Q(D25), .clk(Clock), .clr(Reset));
  Register #(.width(32)) register_27 (.D(IN), .en(R26), .Q(D26), .clk(Clock), .clr(Reset));
  Register #(.width(32)) register_28 (.D(IN), .en(R27), .Q(D27), .clk(Clock), .clr(Reset));
  Register #(.width(32)) register_29 (.D(IN), .en(R28), .Q(D28), .clk(Clock), .clr(Reset));
  Register #(.width(32)) register_30 (.D(IN), .en(R29), .Q(D29), .clk(Clock), .clr(Reset));
  Register #(.width(32)) register_31 (.D(IN), .en(R30), .Q(D30), .clk(Clock), .clr(Reset));
  Register #(.width(32)) register_32 (.D(IN), .en(EN_SP), .Q(D31), .clk(Clock), .clr(Reset));
  and and_2 (and_2_out, GET_INST, POP);
  and and_3 (and_3_out, Lsp, Push);
  or or_1 (EN_SP, R31, and_2_out, and_3_out);
  Multiplexer #(.select(5), .width(32), .enable("false")) multiplexer_2 (
    .in0(D00), .in1(D01), .in2(D02), .in3(D03), .in4(D04), .in5(D05), .in6(D06), .in7(D07), .in8(D08),
    .in9(D09), .in10(D10), .in11(D11), .in12(D12), .in13(D13), .in14(D14), .in15(D15), .in16(D16),
    .in17(D17), .in18(D18), .in19(D19), .in20(D20), .in21(D21), .in22(D22), .in23(D23), .in24(D24),
    .in25(D25), .in26(D26), .in27(D27), .in28(D28), .in29(D29), .in30(D30), .in31(D31), .out(Rs), .sel(SEL_Rs));
  Multiplexer #(.select(5), .width(32), .enable("false")) multiplexer_3 (
    .in0(D00), .in1(D01), .in2(D02), .in3(D03), .in4(D04), .in5(D05), .in6(D06), .in7(D07), .in8(D08),
    .in9(D09), .in10(D10), .in11(D11), .in12(D12), .in13(D13), .in14(D14), .in15(D15), .in16(D16),
    .in17(D17), .in18(D18), .in19(D19), .in20(D20), .in21(D21), .in22(D22), .in23(D23), .in24(D24),
    .in25(D25), .in26(D26), .in27(D27), .in28(D28), .in29(D29), .in30(D30), .in31(D31), .out(Rt), .sel(SEL_Rt));

  // Other names for the same wires on the sheet: C = Clock; DESTINATION_ADDRESS[4:0] = DA; en_H_L = Enable_H_L;
  //   LR = Load_Registers; R = Reset

  // Notes on the sheet:
  //   INPUT
  //   REGISTROS
  //   REGISTER FILE
  //   OUTPUT
endmodule
